// Logisim project bfc.circ as structural Verilog: 5 circuits, main circuit comp
module main (
  input  in_1,
  input  in_2,
  input  [7:0] in_3,
  input  in_4,
  input  [3:0] in_5,
  output out_6,
  output out_7,
  output out_8,
  output out_9,
  output out_10,
  output out_11,
  output out_12,
  output out_13,
  output out_14,
  output out_15
);

  wire and_2_out, and_3_out, d_ff_1_q, demultiplexer_1_out6, demultiplexer_1_out7, demultiplexer_1_out15,
       nor_1_out, nor_2_out, not_1_out, not_2_out, or_1_out;

  D_Flip_Flop d_ff_1 (.clk(or_1_out), .D(or_1_out), .Q(d_ff_1_q), .reset(in_2));  // open: Qn, preset, en
  D_Flip_Flop #(.trigger("high")) d_ff_2 (
    .clk(demultiplexer_1_out15), .D(demultiplexer_1_out15), .Q(out_15), .reset(in_4));  // open: Qn, preset, en
  and and_1 (out_6, in_1, nor_1_out);
  nor nor_1 (nor_1_out, d_ff_1_q, out_15);
  or or_1 (or_1_out, out_13, out_14);
  not not_1 (not_1_out, out_6);
  Demultiplexer #(.select(4), .enable("false")) demultiplexer_1 (
    .out0(out_7), .out1(out_8), .out2(out_9), .out3(out_10), .out4(out_13), .out5(out_14),
    .out6(demultiplexer_1_out6), .out7(demultiplexer_1_out7), .out8(out_12), .out15(demultiplexer_1_out15),
    .in(not_1_out), .sel(in_5));  // open: out9, out10, out11, out12, out13, out14
  not not_2 (not_2_out, nor_2_out);
  and and_2 (and_2_out, demultiplexer_1_out6, nor_2_out);
  and and_3 (and_3_out, demultiplexer_1_out7, not_2_out);
  or or_2 (out_11, and_2_out, and_3_out);
  nor nor_2 (nor_2_out, in_3[0], in_3[1], in_3[2], in_3[3], in_3[5], in_3[6], in_3[7], in_3[4]);
endmodule

module ROM (
  input  in_1,
  input  in_2,
  input  in_3,
  output [7:0] out_4,
  output [3:0] out_5
);

  wire not_1_out, or_1_out;
  wire [11:0] counter_1_q;
  wire [11:8] rom_1_data;

  Counter #(.width(12), .max('hfff)) counter_1 (
    .load(in_1), .D({rom_1_data, out_4}), .count(not_1_out), .Q(counter_1_q), .clk(or_1_out), .clr(in_3));  // open: carry
  not not_1 (not_1_out, in_1);
  or or_1 (or_1_out, in_1, in_2);
  ROM_part #(.addrWidth(12), .dataWidth(16)) rom_1 (
    .addr(counter_1_q), .data({out_5, rom_1_data, out_4}));  // open: sel

  // Notes on the sheet:
  //   contents of rom_1 (hex, n*v repeats v):
  //   200a 600b 3001 1 200a 1 200b 1 2003 1003 7002 1 2001 4000 1 4000 2006 4000 1001 4000 1 3002 4000 1
  //   2002 4000 1001 3004 4000 2007 4000 3008 4000 1001 3003 4000 2003 4000 8000 1 2005 4000 2002 6031
  //   3002 1001 2001 1 702c 1001 4000 8000 2 4000 8000 1003 2001 2 3001 1 5000 4000 300a 605b 3002 1 2006
  //   6049 3001 1001 3006 1 7044 1001 6052 3001 1 2001 1 2001 1002 704b 1001 2001 1 2001 5 5000 4000 300a
  //   7040 1006 605f 1005 705d 1 3001 1003 620b 7 6098 1002 6074 3001 2 606c 5 706a 1001 2001 1004 6072
  //   1005 7070 3 7067 2 6078 5 7076 1002 6087 3001 1003 607f 1005 707d 3 2001 2 6085 5 7083 1002 707a 1
  //   608e 3001 1001 2001 1 7089 1004 3001 1005 6094 1005 7092 5 8000 5 7065 1004 609c 1005 709a 1002 2001
  //   7 60a4 1001 2001 6 70a0 1001 2001 60d9 3001 1002 60b1 3001 1 2001 1 2001 1002 70aa 1001 60ba 3001 1
  //   2001 1 3001 1002 70b3 1 60c1 3001 1001 2001 1 70bc 2 60c8 3001 1002 2001 2 70c3 1001 60d7 8000 1003
  //   60cf 1005 70cd 1002 8000 6 60d5 5 70d3 1001 70ca 1004 70a7 1001 60e0 3001 1001 3001 1 70db 1001 6202
  //   8 60f0 1002 2008 60ec 3001 1001 2006 1 70e7 1001 4000 8 70e4 2008 60fb 3001 1001 2005 1001 2004 1001
  //   2006 3 70f2 1003 4000 1 4000 1 2003 4000 1001 4000 1001 4000 2 2005 610e 3001 1002 3001 2 7109 1001
  //   8000 1003 611e 1003 4000 1 2008 611c 3001 1001 3006 1 7117 1003 7112 200a 6127 3001 1001 2003 1001
  //   2006 2 7120 1001 2002 4000 1001 2001 4000 8000 1 4000 8000 6 6135 5 7133 2001 6139 1005 7137 5 6199
  //   1003 6142 3001 1001 2001 1 713d 1 2001 1002 6150 2 3001 1002 614f 3001 1 2001 1001 714a 7146 1 6157
  //   3001 1001 2001 1 7152 1 615e 2 3001 1002 3001 7159 1001 2009 6182 2 2001 1002 3001 1001 3001 6172 3
  //   3001 1003 6171 3001 2 2001 1002 716c 7168 2 6179 3001 1002 2001 2 7174 1 6180 3001 1 8000 1001 717b
  //   1002 7161 1001 3001 3 2001 1 618f 3001 1001 3001 2 2001 1001 7188 2001 1001 6197 3001 1003 200a 3
  //   7192 6 713b 1005 8000 1 61a4 3001 1001 2001 2 2001 1001 719d 1 61ab 3001 1001 2001 1 71a6 1007 61af
  //   1005 71ad 5 61b3 5 71b1 1005 61d3 1 61c0 3001 1 2001 1 2001 1 2001 1003 71b7 2 61c7 3001 1002 2001 2
  //   71c2 2008 61ce 3001 1 2006 1001 71c9 1 4000 8000 1009 71b5 1 61de 3001 1 2001 1 2001 1 2001 1003
  //   71d5 2 61e5 3001 1002 2001 2 71e0 2008 61ec 3001 1 2006 1001 71e7 1 4000 8000 1 61f3 5 71f1 1005
  //   61f9 1001 2001 1004 71f5 1003 2009 4000 3009 1 2001 1001 3001 70e2 1 6209 3001 1001 2001 1 7204 1001
  //   7063 200a 6216 3001 1 2008 1 200b 1 2006 1003 720d 1 4000 1001 2004 6220 3001 1 2004 1001 721b 1
  //   2001 4000 1 3002 4000 3003 4000 2005 4000 1001 2003 4000 1 2004 4000 3003 4000 3002 4000 1001 2001
  //   4000 2 3002 4000 2002 6241 3002 1003 2001 3 723c 1003 2002 4000 3 2001 6253 3 2008 624f 3001 1001
  //   2006 1 724a 1001 4000 3 7247 200a 4000 ffff
endmodule

module RAM (
  input  in_1,
  input  in_2,
  input  _0,
  input  [7:0] in_4,
  input  SET,
  input  in_6,
  input  in_7,
  input  [7:0] in_8,
  input  N,
  output [7:0] out_10
);

  wire not_1_out, not_2_out, or_1_out, or_2_out, or_3_out;
  wire [7:0] adder_1_out, adder_2_out, and_1_out, bit_extender_1_out, bit_extender_2_out, multiplexer_1_out,
       multiplexer_2_out, not_3_out, register_1_q, xor_1_out;

  assign bit_extender_1_out = {{7{in_2}}, in_2};  // Bit_Extender bit_extender_1
  or or_1 (or_1_out, in_2, in_1);
  Register #(.trigger("falling")) register_1 (.D(adder_1_out), .Q(register_1_q), .clk(or_1_out), .clr(_0));  // open: en
  assign xor_1_out = bit_extender_1_out ^ in_8;  // XOR_Gate xor_1, 8 bits wide
  not not_1 (not_1_out, N);
  Adder adder_1 (.a(register_1_q), .b(xor_1_out), .out(adder_1_out), .cin(in_2));  // open: cout
  Multiplexer #(.width(8), .enable("false")) multiplexer_1 (
    .in0(and_1_out), .in1(in_4), .out(multiplexer_1_out), .sel(SET));
  or or_2 (or_2_out, in_6, N, in_7);
  assign bit_extender_2_out = {{7{not_1_out}}, not_1_out};  // Bit_Extender bit_extender_2
  not not_2 (not_2_out, or_3_out);
  or or_3 (or_3_out, SET, or_2_out);
  RAM_part #(.bus("separate")) ram_1 (
    .addr(register_1_q), .din(multiplexer_1_out), .data(out_10), .clk(not_2_out), .clr(_0));  // open: str, sel, ld
  Multiplexer #(.width(8), .enable("false")) multiplexer_2 (
    .in0(in_8), .in1(not_3_out), .out(multiplexer_2_out), .sel(in_7));
  assign not_3_out = ~in_8;  // NOT_Gate not_3, 8 bits wide
  Adder adder_2 (.a(out_10), .b(multiplexer_2_out), .out(adder_2_out), .cin(in_7));  // open: cout
  assign and_1_out = adder_2_out & bit_extender_2_out;  // AND_Gate and_1, 8 bits wide

  // Notes on the sheet:
  //   NUM
  //   DELTA
endmodule

module Proc (
  input  in_1,
  input  in_2,
  input  in_3,
  input  [6:0] in_4,
  output [6:0] out_5,
  output out_6,
  output out_7,
  output out_8,
  output out_9,
  output out_10,
  output out_11
);

  wire main_1_out_6, main_1_out_7, main_1_out_8, main_1_out_9, main_1_out_10, main_1_out_11, main_1_out_12,
       or_1_out;
  wire [3:0] rom_1_out_5;
  wire [7:0] bit_extender_1_out, rom_1_out_4;
  wire [7:7] ram_1_out_10;

  or or_1 (or_1_out, in_2, out_8, out_6);
  main main_1 (
    .in_1(in_1), .out_13(out_6), .out_14(out_11), .in_2(or_1_out), .out_7(main_1_out_7),
    .out_8(main_1_out_8), .in_3({ram_1_out_10[7], out_5}), .out_9(main_1_out_9), .out_10(main_1_out_10),
    .out_6(main_1_out_6), .in_5(rom_1_out_5), .out_15(out_10), .out_11(main_1_out_11), .in_4(in_2),
    .out_12(main_1_out_12));
  ROM rom_1 (.in_1(main_1_out_11), .in_2(main_1_out_6), .out_5(rom_1_out_5), .in_3(in_2), .out_4(rom_1_out_4));
  RAM ram_1 (
    .in_1(main_1_out_7), .in_2(main_1_out_8), .in_6(main_1_out_9), .in_7(main_1_out_10),
    .out_10({ram_1_out_10[7], out_5}), ._0(in_2), .in_4(bit_extender_1_out), .SET(out_11),
    .in_8(rom_1_out_4), .N(main_1_out_12));
  and and_1 (out_8, out_11, in_3);
  assign bit_extender_1_out = {{1{1'b0}}, in_4};  // Bit_Extender bit_extender_1

  assign out_7 = in_2;
  assign out_9 = in_2;
endmodule

module comp (
);

  wire button_1_out, clock_1_out, keyboard_1_avail, proc_1_out_6, proc_1_out_7, proc_1_out_8, proc_1_out_9,
       proc_1_out_10, proc_1_out_11;
  wire [6:0] keyboard_1_data, proc_1_out_5;

  Clock clock_1 (.out(clock_1_out));
  Button button_1 (.out(button_1_out));
  Proc proc_1 (
    .in_2(button_1_out), .out_5(proc_1_out_5), .out_6(proc_1_out_6), .out_7(proc_1_out_7),
    .in_1(clock_1_out), .out_8(proc_1_out_8), .out_9(proc_1_out_9), .in_4(keyboard_1_data),
    .in_3(keyboard_1_avail), .out_10(proc_1_out_10), .out_11(proc_1_out_11));
  LED led_1 (.in(proc_1_out_10));
  TTY #(.rows(16), .cols(64)) tty_1 (.data(proc_1_out_5), .clk(proc_1_out_6), .clr(proc_1_out_7));  // open: we
  LED led_2 (.in(proc_1_out_11));
  Keyboard #(.trigger("falling")) keyboard_1 (
    .clk(proc_1_out_8), .clr(proc_1_out_9), .avail(keyboard_1_avail), .data(keyboard_1_data));  // open: re

  // Notes on the sheet:
  //   Reset Button
  //   Clock
  //   End program indicator
  //   Press reset button, set clock to 0 and press Ctrl+K
  //   License: CC BY-SA 4.0
  //   Author: Kruchinin Tim
  //   Input indicator
endmodule
